# Fritzing sketch TeensyDRUM-6 (saved by Fritzing 0.9.2b)
circuit board: 8.5cm x 10cm
breadboards: 1

parts:
  Teensy_3_1 = Teensy 3.1
  J3 = double row female pin header, 8 pins [form="♀ (female)"]
  J5 = double row female pin header, 8 pins [form="♀ (female)"]
  J6 = double row female pin header, 8 pins [form="♀ (female)"]
  J7 = double row female pin header, 8 pins [form="♀ (female)"]
  J9 = female pin header, 7 pins [form="♀ (female)"]
  J10 = female pin header, 7 pins [form="♀ (female)"]
  I2C = female pin header, 2 pins [form="♀ (female)"]
  RX1 = female pin header, 2 pins [form="♀ (female)"]
  SIGNAL = female pin header, 3 pins [form="♀ (female)"]
  USB1 = female pin header, 1 pin [form="♀ (female)"]
  -_D+D- = female pin header, 3 pins [form="♀ (female)"]
  78005 = Voltage Regulator [package=to220-igo]
  +_- = female pin header, 2 pins [form="♀ (female)"]
  2_2K = Resistor [tolerance=±5% resistance=220 package=THT]
  2_2K_2 = Resistor [tolerance=±5% resistance=220 package=THT]
  AGND = female pin header, 1 pin [form="♀ (female)"]
  J15 = female pin header, 7 pins [form="♀ (female)"]
  +_-_2 = female pin header, 2 pins [form="♀ (female)"]
  MUX_1 = IC, DIP package, 16 pins [chip_label=IC]
  MUX_6 = IC, DIP package, 16 pins [chip_label=IC]
  MUX_5 = IC, DIP package, 16 pins [chip_label=IC]
  MUX_2 = IC, DIP package, 16 pins [chip_label=IC]
  +_-_3 = female pin header, 2 pins [form="♀ (female)"]
  +_-_4 = female pin header, 2 pins [form="♀ (female)"]
  +_-_5 = female pin header, 2 pins [form="♀ (female)"]
  +_-_6 = female pin header, 2 pins [form="♀ (female)"]
  R18 = Resistor [tolerance=±5% resistance=220 package=THT]
  R19 = Resistor [tolerance=±5% resistance=220 package=THT]
  R21 = Resistor [tolerance=±5% resistance=220 package=THT]
  R22 = Resistor [tolerance=±5% resistance=220 package=THT]
  MUX_3 = IC, DIP package, 16 pins [chip_label=IC]
  +_-_7 = female pin header, 2 pins [form="♀ (female)"]
  J17 = double row female pin header, 8 pins [form="♀ (female)"]
  R23 = Resistor [tolerance=±5% resistance=220 package=THT]
  MUX_4 = IC, DIP package, 16 pins [chip_label=IC]
  J18 = double row female pin header, 8 pins [form="♀ (female)"]
  +_-_8 = female pin header, 2 pins [form="♀ (female)"]
  ANALOG = female pin header, 4 pins [form="♀ (female)"]
  POWER = LED - 5mm [color="Blue (430nm)" package="5 mm [THT]"]
  100 = Resistor [tolerance=±5% resistance=220 package=THT]
  R20 = Resistor [tolerance=±5% resistance=220 package=THT]
  6N138 = IC, DIP package, 8 pins [chip_label=IC]
  220 = Resistor [tolerance=±5% resistance=220 package=THT]
  220_2 = Resistor [tolerance=±5% resistance=220 package=THT]
  RX = female pin header, 2 pins [form="♀ (female)"]
  -_+_TX = female pin header, 2 pins [form="♀ (female)"]
  TX2 = female pin header, 1 pin [form="♀ (female)"]
  220_3 = Resistor [tolerance=±5% resistance=220 package=THT]
  3v3 = female pin header, 4 pins [form="♀ (female)"]
  5v = female pin header, 4 pins [form="♀ (female)"]
  GND = female pin header, 4 pins [form="♀ (female)"]
  DIGITAL_PINS = female pin header, 8 pins [form="♀ (female)"]
  J16 = female pin header, 7 pins [form="♀ (female)"]
  1N4148 = Schottky Diode [part_number=1N41418 package="300 mil [THT]"]
  J12 = female pin header, 3 pins [form="♀ (female)"]

nets:
  GND: Teensy_3_1.GND, -_D+D-.pin1, 78005.GND, +_-.pin1, +_-_2.pin2, MUX_1.pin6, MUX_1.pin7, MUX_1.pin8, MUX_6.pin6, MUX_6.pin7, MUX_6.pin8, MUX_5.pin6, MUX_5.pin7, MUX_5.pin8, MUX_2.pin6, MUX_2.pin7, MUX_2.pin8, +_-_3.pin1, +_-_4.pin1, +_-_5.pin2, +_-_6.pin2, MUX_3.pin6, MUX_3.pin7, MUX_3.pin8, +_-_7.pin2, MUX_4.pin6, MUX_4.pin7, MUX_4.pin8, +_-_8.pin1, 100.Pin_0, 6N138.pin5, -_+_TX.pin1, GND.pin1, GND.pin2, GND.pin3, GND.pin4
  N1: Teensy_3_1.D0, 6N138.pin6, 220_2.Pin_0
  N2: Teensy_3_1.D1, TX2.pin1
  N3: Teensy_3_1.D2, SIGNAL.pin3, MUX_1.pin11, MUX_6.pin11, MUX_5.pin11, MUX_2.pin11, MUX_3.pin11, MUX_4.pin11
  N4: Teensy_3_1.D3, SIGNAL.pin2, MUX_1.pin10, MUX_6.pin10, MUX_5.pin10, MUX_2.pin10, MUX_3.pin10, MUX_4.pin10
  N5: Teensy_3_1.D4, SIGNAL.pin1, MUX_1.pin9, MUX_6.pin9, MUX_5.pin9, MUX_2.pin9, MUX_3.pin9, MUX_4.pin9
  N6: Teensy_3_1.D5, DIGITAL_PINS.pin1
  N7: Teensy_3_1.D6, DIGITAL_PINS.pin2
  N8: Teensy_3_1.D7, DIGITAL_PINS.pin3
  N9: Teensy_3_1.D8, DIGITAL_PINS.pin4
  N10: Teensy_3_1.D9, DIGITAL_PINS.pin5
  N11: Teensy_3_1.D10, DIGITAL_PINS.pin6
  N12: Teensy_3_1.D11, DIGITAL_PINS.pin7
  N13: Teensy_3_1.D12, DIGITAL_PINS.pin8
  N14: Teensy_3_1.3V3, 2_2K.Pin_0, 2_2K_2.Pin_0, 6N138.pin8, 220_2.Pin_1, 3v3.pin1, 3v3.pin2, 3v3.pin3, 3v3.pin4
  N15: Teensy_3_1.D13, USB1.pin1
  N16: Teensy_3_1.A0/D14, R21.Pin_1
  N17: Teensy_3_1.A1/D15, R20.Pin_1
  N18: Teensy_3_1.A2/D16, R22.Pin_1
  N19: Teensy_3_1.A3/D17, R23.Pin_0
  N20: Teensy_3_1.A4/D18, R19.Pin_0
  N21: Teensy_3_1.A5/D19, R18.Pin_0
  N22: Teensy_3_1.A6/D20, ANALOG.pin4
  N23: Teensy_3_1.A7/D21, ANALOG.pin3
  N24: Teensy_3_1.A8/D22, ANALOG.pin2
  N25: Teensy_3_1.A9/D23, ANALOG.pin1
  N26: Teensy_3_1.AGND, AGND.pin1
  N27: Teensy_3_1.Vin, 78005.OUT, +_-_2.pin1, MUX_1.pin16, MUX_6.pin16, MUX_5.pin16, MUX_2.pin16, +_-_3.pin2, +_-_4.pin2, +_-_5.pin1, +_-_6.pin1, MUX_3.pin16, +_-_7.pin1, MUX_4.pin16, +_-_8.pin2, POWER.anode, 220_3.Pin_0, 5v.pin1, 5v.pin2, 5v.pin3, 5v.pin4
  N28: J3.pin1, MUX_2.pin5
  N29: J3.pin2, MUX_2.pin4
  N30: J3.pin3, MUX_2.pin2
  N31: J3.pin4, MUX_2.pin1
  N32: J3.pin5, MUX_2.pin15
  N33: J3.pin6, MUX_2.pin14
  N34: J3.pin7, MUX_2.pin13
  N35: J3.pin8, MUX_2.pin12
  N36: J5.pin1, MUX_1.pin5
  N37: J5.pin2, MUX_1.pin4
  N38: J5.pin3, MUX_1.pin2
  N39: J5.pin4, MUX_1.pin1
  N40: J5.pin5, MUX_1.pin15
  N41: J5.pin6, MUX_1.pin14
  N42: J5.pin7, MUX_1.pin13
  N43: J5.pin8, MUX_1.pin12
  N44: J6.pin1, MUX_6.pin5
  N45: J6.pin2, MUX_6.pin4
  N46: J6.pin3, MUX_6.pin2
  N47: J6.pin4, MUX_6.pin1
  N48: J6.pin5, MUX_6.pin15
  N49: J6.pin6, MUX_6.pin14
  N50: J6.pin7, MUX_6.pin13
  N51: J6.pin8, MUX_6.pin12
  N52: J7.pin1, MUX_5.pin5
  N53: J7.pin2, MUX_5.pin4
  N54: J7.pin3, MUX_5.pin2
  N55: J7.pin4, MUX_5.pin1
  N56: J7.pin5, MUX_5.pin15
  N57: J7.pin6, MUX_5.pin14
  N58: J7.pin7, MUX_5.pin13
  N59: J7.pin8, MUX_5.pin12
  N60: J9.pin1, J16.pin1
  N61: J9.pin2, J16.pin2
  N62: J9.pin3, J16.pin3
  N63: J9.pin4, J16.pin4
  N64: J9.pin5, J16.pin5
  N65: J9.pin6, I2C.pin2, 2_2K.Pin_1, J16.pin6
  N66: J9.pin7, I2C.pin1, 2_2K_2.Pin_1, J16.pin7
  N67: J10.pin1, J15.pin1
  N68: J10.pin2, J15.pin2
  N69: J10.pin3, J15.pin3
  N70: J10.pin4, J15.pin4
  N71: J10.pin5, J15.pin5
  N72: J10.pin6, J15.pin6
  N73: J10.pin7, J15.pin7
  N74: RX1.pin1, -_D+D-.pin3, J12.pin2
  N75: RX1.pin2, -_D+D-.pin2, J12.pin1
  N76: 78005.IN, +_-.pin2
  N77: MUX_1.pin3, R21.Pin_0
  N78: MUX_6.pin3, R18.Pin_1
  N79: MUX_5.pin3, R19.Pin_1
  N80: MUX_2.pin3, R20.Pin_0
  N81: R22.Pin_0, MUX_3.pin3
  N82: MUX_3.pin1, J17.pin4
  N83: MUX_3.pin2, J17.pin3
  N84: MUX_3.pin4, J17.pin2
  N85: MUX_3.pin5, J17.pin1
  N86: MUX_3.pin12, J17.pin8
  N87: MUX_3.pin13, J17.pin7
  N88: MUX_3.pin14, J17.pin6
  N89: MUX_3.pin15, J17.pin5
  N90: R23.Pin_1, MUX_4.pin3
  N91: MUX_4.pin1, J18.pin4
  N92: MUX_4.pin2, J18.pin3
  N93: MUX_4.pin4, J18.pin2
  N94: MUX_4.pin5, J18.pin1
  N95: MUX_4.pin12, J18.pin8
  N96: MUX_4.pin13, J18.pin7
  N97: MUX_4.pin14, J18.pin6
  N98: MUX_4.pin15, J18.pin5
  N99: POWER.cathode, 100.Pin_1
  N100: 6N138.pin2, 220.Pin_1, 1N4148.cathode
  N101: 6N138.pin3, RX.pin2, 1N4148.anode
  N102: 220.Pin_0, RX.pin1
  N103: -_+_TX.pin2, 220_3.Pin_1
